# Fritzing sketch layout (saved by Fritzing 0.7.10b)
breadboards: 1

parts:
  Arduino1 = Arduino
  J2 = Basic Servo
  LED1 = LED - 5mm [color="Green (555nm)" package="5 mm [THT]"]
  LED2 = LED - 5mm [color="Red (633nm)" part_number="Laser Pointer" package="5 mm [THT]"]
  KEYPAD1 = Membrane Matrix Keypad
  C1 = Ceramic Capacitor [capacitance=10pF voltage=16V package="100 mil [THT, multilayer]"]
  C3 = Electrolytic Capacitor [capacitance=10µF voltage=16V package="100 mil [THT, electrolytic]"]
  C4 = Ceramic Capacitor [capacitance=10pF voltage=16V package="100 mil [THT, multilayer]"]
  C5 = Ceramic Capacitor [capacitance=10pF package="100 mil [THT, multilayer]"]
  Q1 = NPN-Transistor [package="TO92 [THT]"]
  U1 = Voltage Regulator - 5V [part_number=29300-5.0WT package="TO220 [THT]"]
  VCC1 = Battery block 9V
  Fuse1 = Fuse with Handler [part_number=XF050]
  R2 = Resistor [tolerance=±5% resistance=330 package=THT]
  C6 = Electrolytic Capacitor [capacitance=0.1mF voltage=16V package="100 mil [THT, electrolytic]"]
  C7 = Ceramic Capacitor [capacitance=0.1µF voltage=16V package="100 mil [THT, multilayer]"]
  J3 = Basic Servo
  R3 = Resistor [tolerance=±5% resistance=33 package=THT]
  C9 = Electrolytic Capacitor [capacitance=1mF voltage=16V package="100 mil [THT, electrolytic]"]
  C8 = Electrolytic Capacitor [capacitance=0.1mF voltage=35V package="200 mil [THT, electrolytic]"]

nets (from the schematic view):
  N1: Arduino1.D12, Q1.B
  N2: Arduino1.D11, R2.Pin_1
  N3: Arduino1.D10, J2.pulse
  N4: Arduino1.D9, J3.pulse
  N5: Arduino1.D8, KEYPAD1.7
  N6: Arduino1.D7, KEYPAD1.6
  N7: Arduino1.D6, KEYPAD1.5
  N8: Arduino1.D5, KEYPAD1.4
  N9: Arduino1.D4, KEYPAD1.3
  N10: Arduino1.D3, KEYPAD1.2
  N11: Arduino1.D2, KEYPAD1.1
  5V: Arduino1.VIN, J2.vcc, C1.1, C3.+, C4.0, C5.0, Q1.C, U1.output_voltage, C6.+, C7.1, J3.vcc, C9.+
  GND: J2.gnd, LED1.cathode, LED2.cathode, C1.0, C3.-, C4.1, C5.1, U1.GND, VCC1.-, C6.-, C7.0, J3.gnd, C9.-, C8.-
  N12: LED1.anode, R2.Pin_0
  N13: LED2.anode, R3.Pin_1
  N14: Q1.E, R3.Pin_0
  N15: U1.input_voltage, Fuse1.Connector1, C8.+

custom parts:
  Membrane Matrix Keypad: Membrane Matrix 3x4 Keypad
